# Fritzing sketch HeimdallPad Circuits (saved by Fritzing 0.9.3b)
perfboards: 2
breadboards: 3

parts:
  LED4 = LED - 5mm [color="Yellow (595nm)" package="5 mm [THT]"]
  LED5 = LED - 5mm [color="Red (633nm)" package="5 mm [THT]"]
  LED6 = LED - 5mm [color="Green (555nm)" package="5 mm [THT]"]
  S10 = Pushbutton [package="[THT]"]
  R26 = Resistor [tolerance=±5% resistance=10 package=THT]
  VCC2 = Battery
  U3 = atmega328 [package=dip]
  R30 = Resistor [tolerance=±5% resistance=2k package=THT]
  R31 = Resistor [tolerance=±5% resistance=4.7k package=THT]
  Espessif_Serial_Wifi_Modul_3 = ESP8266 ESP01 [part_number=ESP8266 package=THT]
  S11 = Pushbutton [package="[THT]"]
  S12 = Pushbutton [package="[THT]"]
  S13 = Pushbutton [package="[THT]"]
  S14 = Pushbutton [package="[THT]"]
  Q1 = NPN-Transistor [package="TO92 [THT]"]
  IC1 = Voltage Regulator [package=to-92]
  LED7 = smd LED [color="Blue (430nm)" package="0603 [SMD]"]
  R32 = Resistor [tolerance=±5% resistance=10 package=THT]
  R33 = Resistor [tolerance=±5% resistance=330 package="1206 [SMD]"]
  D1 = Diode [package=diode-hv]
  D2 = Diode [package=diode-hv]
  D3 = Diode [package=diode-hv]
  D4 = Diode [package=diode-hv]
  D5 = Diode [package=diode-hv]
  S15 = Pushbutton [package="[THT]"]
  S16 = Pushbutton [package="[THT]"]

nets:
  N1: LED4.cathode, U3.D7
  N2: LED5.cathode, U3.D5_(PWM)
  N3: LED5.anode, R32.Pin_1
  N4: LED6.cathode, U3.D6_(PWM)
  N5: S10.Pin_1, S10.Pin_2
  N6: S10.Pin_3, S10.Pin_4, U3.D13, D2.C
  N7: R26.Pin_0, VCC2.+, IC1.OUT
  N8: R26.Pin_1, LED7.anode
  N9: VCC2.-, Q1.E
  N10: U3.RESET, S11.Pin_3, S11.Pin_4
  N11: U3.D8, R33.Pin_0
  N12: U3.D9_(PWM), S14.Pin_3, S14.Pin_4, D4.C
  N13: U3.D10_(PWM), S13.Pin_3, S13.Pin_4, D1.C
  N14: U3.D11_(PWM), S12.Pin_3, S12.Pin_4, D3.C
  N15: U3.A2, D5.C, S15.Pin_3, S15.Pin_4
  N16: U3.A3, LED7.cathode
  N17: U3.A4, R30.Pin_0
  N18: U3.A5, Espessif_Serial_Wifi_Modul_3.TXD
  N19: R30.Pin_1, R31.Pin_0, Espessif_Serial_Wifi_Modul_3.RXD
  N20: Espessif_Serial_Wifi_Modul_3.GND, Q1.B
  N21: Espessif_Serial_Wifi_Modul_3.VCC, Espessif_Serial_Wifi_Modul_3.CH_PD, IC1.IN
  N22: S11.Pin_1, S11.Pin_2
  N23: S12.Pin_1, S12.Pin_2
  N24: S13.Pin_1, S13.Pin_2
  N25: S14.Pin_1, S14.Pin_2
  N26: Q1.C, R33.Pin_1
  N27: S15.Pin_1, S15.Pin_2
  N28: S16.Pin_1, S16.Pin_2
  N29: S16.Pin_3, S16.Pin_4

custom parts:
  ESP8266 ESP01: Generic WiFi Module based on the ESP8266 with onboard PCB antenna and UART communications
